# Fritzing sketch esp8266-dht11-sensor-circuit-diagram (saved by Fritzing 0.9.4)
breadboards: 1

parts:
  WeMos_D1_Mini1 = WeMos D1 Mini
  DHT1 = DHT11 Humitidy and Temperature Sensor
  R1 = Resistor [tolerance=±5% resistance=10k package=THT]

nets:
  3V3: WeMos_D1_Mini1.3V3, DHT1.VDD, R1.Pin_1
  N1: WeMos_D1_Mini1.D1, DHT1.DATA, R1.Pin_0
  N2: WeMos_D1_Mini1.G, DHT1.GND

custom parts:
  DHT11 Humitidy and Temperature Sensor: DHT11 Humidity and Temperature Sensor
